// Logisim project simon_says.circ as structural Verilog: 1 circuit, main circuit main
module main (
);

  wire clock_1_out, clock_2_out, dipswitch_1_p1, dipswitch_1_p2, dipswitch_1_p3, dipswitch_1_p4,
       dipswitch_2_p1, dipswitch_2_p2, dipswitch_2_p3, dipswitch_2_p4, register_7_q;

  Clock clock_1 (.out(clock_1_out));
  Clock clock_2 (.out(clock_2_out));
  Register #(.width(1)) register_1 (.D(dipswitch_1_p1), .en(1'b1), .clk(clock_1_out), .clr(1'b0));  // open: Q
  Register #(.width(1)) register_2 (.D(dipswitch_2_p1), .en(1'b1), .clk(clock_2_out), .clr(1'b0));  // open: Q
  // DipSwitch #(.number(4)) dipswitch_1: pin names not known; wires that end beside it: dipswitch_1_p1, dipswitch_1_p2, dipswitch_1_p3, dipswitch_1_p4
  // DipSwitch #(.number(4)) dipswitch_2: pin names not known; wires that end beside it: dipswitch_2_p1, dipswitch_2_p2, dipswitch_2_p3, dipswitch_2_p4
  Register #(.width(1)) register_3 (.D(dipswitch_1_p2), .en(1'b1), .clk(clock_1_out), .clr(1'b0));  // open: Q
  Register #(.width(1)) register_4 (.D(dipswitch_2_p2), .en(1'b1), .clk(clock_2_out), .clr(1'b0));  // open: Q
  Register #(.width(1)) register_5 (.D(dipswitch_2_p3), .en(1'b1), .clk(clock_2_out), .clr(1'b0));  // open: Q
  Register #(.width(1)) register_6 (.D(dipswitch_1_p3), .en(1'b1), .clk(clock_1_out), .clr(1'b0));  // open: Q
  Register #(.width(1)) register_7 (.D(dipswitch_1_p4), .en(1'b1), .clk(clock_1_out), .Q(register_7_q), .clr(1'b0));
  Register #(.width(1)) register_8 (.D(dipswitch_2_p4), .en(1'b1), .clk(clock_2_out), .clr(1'b0));  // open: Q

  // Notes on the sheet:
  //   User
  //   Simon
endmodule
